# Fritzing sketch SuperCollider-SerialCtl (saved by Fritzing 0.9.6b)
breadboards: 1

parts:
  Teensy_3_1 = Teensy 3.1  # not connected
  R1 = Rotary Potentiometer (Large) [maximum_resistance=10kΩ package=THT]
  R2 = Rotary Potentiometer (Large) [maximum_resistance=10kΩ package=THT]
  R3 = Rotary Potentiometer (Large) [maximum_resistance=10kΩ package=THT]
  R4 = Rotary Potentiometer (Large) [maximum_resistance=10kΩ package=THT]
  S1 = Toggle Switch [package=THT]
  S2 = Toggle Switch [package=THT]
  S3 = Toggle Switch [package=THT]

nets:
  N1: R1.leg1, R2.leg1, R3.leg1, R4.leg1, S1.L1, S2.L1, S3.L1
  N2: R1.leg2, R2.leg2, R3.leg2, R4.leg2
